# Fritzing sketch LCD_Temp_Moisture Diagram (saved by Fritzing 0.9.3b)
breadboards: 1

parts:
  Part1 = Arduino Uno (Rev3)
  Part2 = Soil Moisture Sensor
  LCD1 = LCD screen
  RHT1 = Humidity and Temperature Sensor RHT03

nets:
  N1: Part1.A0, RHT1.Data-signal
  N2: Part1.A1, Part2.SIG
  N3: Part1.D9_PWM, LCD1.V0
  N4: Part1.D11_PWM/MOSI, LCD1.E
  N5: Part1.D12/MISO, LCD1.RS
  GND: Part1.GND, Part2.GND, LCD1.VSS, RHT1.GND_2
  N6: Part1.D2, LCD1.DB7
  N7: Part1.D3_PWM, LCD1.DB6
  N8: Part1.D4, LCD1.DB5
  N9: Part1.D5_PWM, LCD1.DB4
  VCC: Part1.3V3, Part2.VCC, RHT1.Vcc
  5V: Part1.5V, LCD1.VDD
